# Fritzing sketch webmididash (saved by Fritzing 0.9.3b)

parts:
  Part2 = Arduino Micro (Rev3)
  S1 = Momentary Switch [package=ksa_sealed_tac_switch]
  S2 = Toggle Switch [package=THT]

nets:
  N1: Part2.GND, S1.2, S2.COM
  N2: Part2.D2/SDA, S1.4
  N3: Part2.D3/SCL, S2.L1
